# Fritzing sketch Sketch_SmrtMultiTab (saved by Fritzing 0.9.3b)
breadboards: 1

parts:
  U1 = NodeMCU V1.0
  DHT1 = DHT11 Humitidy and Temperature Sensor

nets:
  3V3: U1.3V3, DHT1.VDD
  GND: U1.GND, DHT1.GND
  N1: U1.D5, DHT1.DATA

custom parts:
  NodeMCU V1.0: ESP8266 based NodeMCU
  DHT11 Humitidy and Temperature Sensor: DHT11 Humidity and Temperature Sensor
